# Fritzing sketch device (saved by Fritzing 0.6.4b)
breadboards: 1

parts:
  K2 = LH1500AT_Solid_State_Relay_DIP_6
  K1 = LH1500AT_Solid_State_Relay_DIP_6
  DS18B20_5 = Maxim___Dallas_18B20_Temperature_Sensor [part_number="DS18B20\r"]
  DS18B20_4 = Maxim___Dallas_18B20_Temperature_Sensor [part_number="DS18B20\r"]
  DS18B20_3 = Maxim___Dallas_18B20_Temperature_Sensor [part_number="DS18B20\r"]
  DS18B20_2 = Maxim___Dallas_18B20_Temperature_Sensor [part_number="DS18B20\r"]
  DS18B20_1 = Maxim___Dallas_18B20_Temperature_Sensor [part_number="DS18B20\r"]
  U1 = Voltage Regulator - 5V [package="TO220 [THT]"]
  POWERPLUG1 = Power plug
  M1_Water_Pump = DC Motor
  R1 = Resistor [tolerance=±5% resistance=220 package="1206 [SMD]"]
  QUICKSTART_PROPELLER1 = P8X32A_QuickStart [part_number=40000]
  U2 = Voltage Regulator - 5V [package="TO220 [THT]"]
  U3 = Voltage Regulator - 5V [package="TO220 [THT]"]
  U4 = Voltage Regulator - 5V [package="TO220 [THT]"]
  C1 = Ceramic Capacitor [capacitance=10µF voltage=20V package="100 mil [THT, multilayer]"]

nets:
  N1: K2.connector0, QUICKSTART_PROPELLER1.connector14
  GND: K2.connector1, K1.connector1, DS18B20_5.connector3, DS18B20_4.connector3, DS18B20_3.connector3, DS18B20_2.connector3, DS18B20_1.connector3, U1.GND, POWERPLUG1.GND, M1_Water_Pump.pin_1, R1.Pin_0, QUICKSTART_PROPELLER1.connector18, U2.GND, U3.GND, U4.GND, C1.1
  N2: K2.connector3, M1_Water_Pump.pin_2
  N3: K2.connector5, U1.output_voltage, QUICKSTART_PROPELLER1.connector19, U2.output_voltage, U3.output_voltage, U4.output_voltage
  N4: K1.connector0, QUICKSTART_PROPELLER1.connector13
  N5: K1.connector3, R1.Pin_1
  N6: K1.connector5, U1.input_voltage, POWERPLUG1.VCC, U2.input_voltage, U3.input_voltage, U4.input_voltage, C1.0
  N7: DS18B20_5.connector4, QUICKSTART_PROPELLER1.connector12
  N8: DS18B20_5.connector5, DS18B20_4.connector5, DS18B20_3.connector5, DS18B20_2.connector5, DS18B20_1.connector5, QUICKSTART_PROPELLER1.connector17
  N9: DS18B20_4.connector4, QUICKSTART_PROPELLER1.connector11
  N10: DS18B20_3.connector4, QUICKSTART_PROPELLER1.connector10
  N11: DS18B20_2.connector4, QUICKSTART_PROPELLER1.connector9
  N12: DS18B20_1.connector4, QUICKSTART_PROPELLER1.connector8
